# Fritzing sketch pilot (saved by Fritzing 1.0.5)
breadboards: 2

parts:
  Part1 = Arduino Nano (Rev3.0)
  S1 = Pushbutton [package="[THT]"]
  S3 = Pushbutton [package="[THT]"]
  S4 = Pushbutton [package="[THT]"]
  R1 = Resistor [tolerance=±5% power=0.25W resistance=10k package=THT]
  AMS1 = AMS1777 5V regulator module
  U2 = ESP8266 ESP-01 Upgraded WiFi Module [part_number=ESP8266]
  R2 = Resistor [tolerance=±5% power=0.25W resistance=10k package=THT]
  R3 = Resistor [tolerance=±5% power=0.25W resistance=10k package=THT]
  R4 = Resistor [tolerance=±5% power=0.25W resistance=10k package=THT]
  R5 = Resistor [tolerance=±5% power=0.25W resistance=10k package=THT]
  R6 = Resistor [tolerance=±5% power=0.25W resistance=10k package=THT]
  R7 = Resistor [tolerance=±5% power=0.25W resistance=10k package=THT]
  R8 = Resistor [tolerance=±5% power=0.25W resistance=10k package=THT]
  S5 = Pushbutton [package="[THT]"]
  C1 = Ceramic Capacitor [capacitance=100nF voltage=35V package="100 mil [THT, multilayer]"]
  C2 = Ceramic Capacitor [capacitance=100nF voltage=35V package="100 mil [THT, multilayer]"]
  C3 = Ceramic Capacitor [capacitance=100nF voltage=35V package="100 mil [THT, multilayer]"]
  C4 = Ceramic Capacitor [capacitance=100nF voltage=35V package="100 mil [THT, multilayer]"]

nets:
  N1: Part1.GND, S1.Pin_1, S1.Pin_2, S3.Pin_3, S3.Pin_4, S4.Pin_3, S4.Pin_4, AMS1.GND-_(input), S5.Pin_1, S5.Pin_2, C1.0, C3.0, C4.0
  N2: Part1.D2, U2.RXD
  N3: Part1.D3, U2.TXD
  N4: Part1.D5, R7.Pin_0, C3.1
  N5: Part1.D7, R6.Pin_0, C2.0
  N6: Part1.D11/MOSI, R8.Pin_1, C1.1
  N7: Part1.D12/MISO, R5.Pin_1, C4.1
  N8: Part1.5V, R1.Pin_1, AMS1.VIN+, R2.Pin_1, R3.Pin_1, R4.Pin_1, C2.1
  N9: S1.Pin_3, S1.Pin_4, R1.Pin_0, R5.Pin_0
  N10: S3.Pin_1, S3.Pin_2, R3.Pin_0, R6.Pin_1
  N11: S4.Pin_1, S4.Pin_2, R4.Pin_0, R7.Pin_1
  N12: AMS1.VOUT+, U2.VCC
  N13: AMS1.GND-_(output), U2.GND
  N14: R2.Pin_0, R8.Pin_0, S5.Pin_3, S5.Pin_4

custom parts:
  AMS1777 5V regulator module: AMS1777 5V regulator module source : https://github.com/ShenTengTu/fritzing_parts/tree/master/voltage%20regulator/AMS1117_5V_regulator_module
  ESP8266 ESP-01 Upgraded WiFi Module: Upgraded Version ESP-01,all Flash are upgraded to 1M byte.Also support Cloud service remote transmission.
